// Logisim project Guia_0501.circ as structural Verilog: 1 circuit, main circuit main
module main (
  input  x,
  input  y,
  output a,
  output b
);

  wire not_1_out, not_2_out;

  not not_1 (not_1_out, x);
  not not_2 (not_2_out, y);
  nor nor_1 (b, y, x);
  and and_1 (a, not_1_out, not_2_out);

  // Notes on the sheet:
  //   Guia_0501$David de Sa Vieira de Faria$699415
endmodule
