// Logisim project Guia_0502.circ as structural Verilog: 1 circuit, main circuit main
module main (
  input  a,
  input  b,
  output s,
  output s_2
);

  wire nand_1_out, not_1_out;

  not not_1 (not_1_out, a);
  nand nand_1 (nand_1_out, b, b);
  or or_1 (s, not_1_out, b);
  nand nand_2 (s_2, a, nand_1_out);

  // Notes on the sheet:
  //   Guia_0502$David de Sa Vieira de Faria$699415
endmodule
