// Logisim project Guia_0503.circ as structural Verilog: 1 circuit, main circuit main
module main (
  input  x,
  input  y,
  output a,
  output b
);

  wire nor_1_out, nor_2_out, not_1_out;

  not not_1 (not_1_out, y);
  nor nor_1 (nor_1_out, y, y);
  or or_1 (a, x, not_1_out);
  nor nor_2 (nor_2_out, x, nor_1_out);
  nor nor_3 (b, nor_2_out, nor_2_out);

  // Notes on the sheet:
  //   Guia_0503$David de Sa Vieira de Faria$699415
endmodule
