// Logisim project Guia_0504.circ as structural Verilog: 1 circuit, main circuit main
module main (
  input  x,
  input  y,
  output a,
  output b
);

  wire nand_1_out, nand_2_out, not_1_out;

  not not_1 (not_1_out, x);
  nand nand_1 (nand_1_out, x, x);
  and and_1 (a, not_1_out, y);
  nand nand_2 (nand_2_out, nand_1_out, y);
  nand nand_3 (b, nand_2_out, nand_2_out);

  // Notes on the sheet:
  //   Guia_0504$David de Sa Vieira de Faria$699415
  //   nand_1
  //   nand_2
endmodule
