// Logisim project Guia_0505.circ as structural Verilog: 1 circuit, main circuit main
module main (
  input  x,
  input  y,
  output a,
  output b
);

  wire nor_1_out, nor_2_out, nor_3_out;

  xnor xnor_1 (a, x, y);
  nor nor_1 (nor_1_out, x, y);
  nor nor_2 (nor_2_out, x, nor_1_out);
  nor nor_3 (nor_3_out, nor_1_out, y);
  nor nor_4 (b, nor_2_out, nor_3_out);

  // Notes on the sheet:
  //   Guia_0505$David de Sa Vieira de Faria$699415
endmodule
