// Logisim project Guia_0506.circ as structural Verilog: 1 circuit, main circuit main
module main (
  input  x,
  input  y,
  output a,
  output b
);

  wire nand_1_out, nand_2_out, nand_3_out;

  xor xor_1 (a, x, y);
  nand nand_1 (nand_1_out, x, y);
  nand nand_2 (nand_2_out, x, nand_1_out);
  nand nand_3 (nand_3_out, nand_1_out, y);
  nand nand_4 (b, nand_2_out, nand_3_out);

  // Notes on the sheet:
  //   Guia_0506$David de Sa Vieira de Faria$699415
endmodule
