// Logisim project Guia0601a.circ as structural Verilog: 1 circuit, main circuit main
module main (
  input  X,
  input  Y,
  input  Z,
  output s
);

  wire and_1_out, and_2_out, not_1_out;

  not not_1 (not_1_out, Y);
  and and_1 (and_1_out, Z, not_1_out);
  and and_2 (and_2_out, X, Z);
  or or_1 (s, and_1_out, and_2_out);

  // Notes on the sheet:
  //   Guia_0601a
  //   Nome: David de Sa Vieira de Faria
  //   Matricula: 699415
  //   w3
  //   w1
  //   w2
endmodule
