// Logisim project Guia0601c.circ as structural Verilog: 1 circuit, main circuit main
module main (
  input  X,
  input  Y,
  input  Z,
  output s
);

  wire and_1_out, and_2_out, and_3_out, not_1_out, not_2_out;

  not not_1 (not_1_out, Z);
  not not_2 (not_2_out, Z);
  and and_1 (and_1_out, X, not_1_out);
  and and_2 (and_2_out, X, Y);
  and and_3 (and_3_out, Y, not_2_out);
  or or_1 (s, and_1_out, and_2_out, and_3_out);

  // Notes on the sheet:
  //   Guia_0601c
  //   Nome: David de Sa Vieira de Faria
  //   Matricula: 699415
  //   w4
  //   w5
  //   w1
  //   w2
  //   w3
endmodule
