// Logisim project Guia0602c.circ as structural Verilog: 1 circuit, main circuit main
module main (
  input  X,
  input  Y,
  input  Z,
  output out_4
);

  wire and_1_out, not_1_out, not_2_out, not_3_out, or_1_out, or_2_out, or_3_out;

  not not_1 (not_1_out, Z);
  not not_2 (not_2_out, Y);
  not not_3 (not_3_out, X);
  or or_1 (or_1_out, X, Y, not_1_out);
  or or_2 (or_2_out, not_2_out, Z);
  or or_3 (or_3_out, not_3_out, Z);
  and and_1 (and_1_out, or_1_out, or_2_out);
  and and_2 (out_4, and_1_out, or_3_out);

  // Notes on the sheet:
  //   Guia_0602c
  //   Nome: David de Sa Vieira de Faria
  //   Matricula: 699415
endmodule
