// Logisim project Guia0602d.circ as structural Verilog: 1 circuit, main circuit main
module main (
  input  X,
  input  Y,
  input  Z,
  output out_4
);

  wire not_1_out, not_2_out, not_3_out, or_1_out, or_2_out;

  not not_1 (not_1_out, Z);
  not not_2 (not_2_out, X);
  not not_3 (not_3_out, Z);
  or or_1 (or_1_out, X, not_1_out);
  or or_2 (or_2_out, not_2_out, not_3_out);
  and and_1 (out_4, or_1_out, or_2_out);

  // Notes on the sheet:
  //   Guia_0602d
  //   Nome: David de Sa Vieira de Faria
  //   Matricula: 699415
endmodule
