// Logisim project Guia0603a.circ as structural Verilog: 1 circuit, main circuit main
module main (
  input  A,
  input  B,
  input  C,
  input  D,
  output s
);

  wire and_1_out, and_2_out, and_3_out, not_1_out, not_2_out, not_3_out, not_4_out, not_5_out, not_6_out;

  not not_1 (not_1_out, A);
  not not_2 (not_2_out, C);
  not not_3 (not_3_out, B);
  not not_4 (not_4_out, D);
  not not_5 (not_5_out, C);
  not not_6 (not_6_out, D);
  and and_1 (and_1_out, not_1_out, not_2_out, D);
  and and_2 (and_2_out, not_3_out, C, not_4_out);
  and and_3 (and_3_out, A, not_5_out, not_6_out);
  or or_1 (s, and_1_out, and_2_out, and_3_out);

  // Notes on the sheet:
  //   Guia_0603a
  //   Nome: David de Sa Vieira de Faria
  //   Matricula: 699415
  //   w5
  //   w6
  //   w1
  //   w2
  //   w3
  //   w8
  //   w4
  //   w7
  //   w9
endmodule
