// Logisim project Guia0603d.circ as structural Verilog: 1 circuit, main circuit main
module main (
  input  A,
  input  B,
  input  C,
  input  D,
  output s
);

  wire and_1_out, and_2_out, and_3_out, and_4_out, and_5_out, not_1_out, not_2_out, not_3_out, not_4_out,
       not_5_out, not_6_out, not_7_out;

  not not_1 (not_1_out, A);
  not not_2 (not_2_out, C);
  not not_3 (not_3_out, A);
  not not_4 (not_4_out, C);
  not not_5 (not_5_out, B);
  not not_6 (not_6_out, D);
  not not_7 (not_7_out, D);
  and and_1 (and_1_out, not_1_out, B, not_2_out);
  and and_2 (and_2_out, not_3_out, B, D);
  and and_3 (and_3_out, B, not_4_out, D);
  and and_4 (and_4_out, not_5_out, C, not_6_out);
  and and_5 (and_5_out, A, C, not_7_out);
  or or_1 (s, and_1_out, and_2_out, and_3_out, and_4_out, and_5_out);

  // Notes on the sheet:
  //   Guia_0603c
  //   Nome: David de Sa Vieira de Faria
  //   Matricula: 699415
  //   na
  //   na
  //   na
  //   w1
  //   w2
  //   w3
  //   nc
  //   nd
  //   nd
  //   w4
  //   w5
endmodule
