// Logisim project Guia0603e.circ as structural Verilog: 1 circuit, main circuit main
module main (
  input  A,
  input  B,
  input  C,
  input  D,
  output s
);

  wire and_1_out, and_2_out, not_1_out, not_2_out;

  not not_1 (not_1_out, B);
  not not_2 (not_2_out, C);
  and and_1 (and_1_out, not_1_out, not_2_out);
  and and_2 (and_2_out, C, D);
  or or_1 (s, and_1_out, and_2_out);

  // Notes on the sheet:
  //   Guia_0603e
  //   Nome: David de Sa Vieira de Faria
  //   Matricula: 699415
  //   nb
  //   nc
  //   w1
  //   w1
endmodule
