// Logisim project Guia0604a.circ as structural Verilog: 2 circuits, main circuit main
module main (
  input  A,
  input  B,
  input  C,
  input  D,
  output s
);

  wire not_1_out, not_2_out, not_3_out, not_4_out, not_5_out, or_1_out, or_2_out, or_3_out;

  not not_1 (not_1_out, B);
  not not_2 (not_2_out, D);
  not not_3 (not_3_out, B);
  not not_4 (not_4_out, D);
  not not_5 (not_5_out, C);
  or or_1 (or_1_out, A, not_1_out, not_2_out);
  or or_2 (or_2_out, not_3_out, C, not_4_out);
  or or_3 (or_3_out, A, B, not_5_out, D);
  and and_1 (s, or_1_out, or_2_out, or_3_out);

  // Notes on the sheet:
  //   Guia_0604a
  //   Nome: David de Sa Vieira de Faria
  //   Matricula: 699415
  //   nb
  //   nd
  //   nb
  //   nd
  //   nc
  //   w1
  //   w2
  //   w2
endmodule

module not_wire (
);

  wire not_1_out, not_2_out, not_3_out, not_4_out;

  // NOT_Gate not_1 has open pins: in=open, out=not_1_out
  // NOT_Gate not_2 has open pins: in=open, out=not_2_out
  // NOT_Gate not_3 has open pins: in=open, out=not_3_out
  // NOT_Gate not_4 has open pins: in=open, out=not_4_out

  // Notes on the sheet:
  //   na
  //   nb
  //   nc
  //   nd
  //   w1
endmodule
