// Logisim project Guia0604b.circ as structural Verilog: 1 circuit, main circuit main
module main (
  input  A,
  input  B,
  input  C,
  input  D,
  output s
);

  wire not_1_out, not_2_out, not_3_out, not_4_out, not_5_out, not_6_out, or_1_out, or_2_out, or_3_out;

  not not_1 (not_1_out, B);
  not not_2 (not_2_out, A);
  not not_3 (not_3_out, A);
  not not_4 (not_4_out, B);
  not not_5 (not_5_out, C);
  not not_6 (not_6_out, D);
  or or_1 (or_1_out, not_1_out, C, D);
  or or_2 (or_2_out, not_2_out, B, C);
  or or_3 (or_3_out, not_3_out, not_4_out, not_5_out, not_6_out);
  and and_1 (s, or_1_out, or_2_out, or_3_out);

  // Notes on the sheet:
  //   Guia_0604b
  //   Nome: David de Sa Vieira de Faria
  //   Matricula: 699415
  //   nb
  //   na
  //   na
  //   nb
  //   nc
  //   nd
  //   w1
  //   w2
  //   w2
endmodule
