// Logisim project Guia0604c.circ as structural Verilog: 1 circuit, main circuit main
module main (
  input  A,
  input  B,
  input  C,
  input  D,
  output s
);

  wire not_1_out, not_2_out, not_3_out, not_4_out, not_5_out, not_6_out, not_7_out, not_8_out, or_1_out,
       or_2_out, or_3_out, or_4_out;

  not not_1 (not_1_out, A);
  not not_2 (not_2_out, C);
  not not_3 (not_3_out, D);
  not not_4 (not_4_out, A);
  not not_5 (not_5_out, B);
  not not_6 (not_6_out, D);
  not not_7 (not_7_out, B);
  not not_8 (not_8_out, A);
  or or_1 (or_1_out, not_1_out, not_2_out, not_3_out);
  or or_2 (or_2_out, not_4_out, not_5_out, not_6_out);
  or or_3 (or_3_out, A, not_7_out, C, D);
  or or_4 (or_4_out, not_8_out, B, C, D);
  and and_1 (s, or_1_out, or_2_out, or_3_out, or_4_out);

  // Notes on the sheet:
  //   Guia_0604c
  //   Nome: David de Sa Vieira de Faria
  //   Matricula: 699415
  //   na
  //   nc
  //   nd
  //   na
  //   nb
  //   nd
  //   nb
  //   na
  //   w1
  //   w2
  //   w3
  //   w4
endmodule
