// Logisim project Guia0604d.circ as structural Verilog: 1 circuit, main circuit main
module main (
  input  A,
  input  B,
  input  C,
  input  D,
  output s
);

  wire not_1_out, not_2_out, not_3_out, not_4_out, not_5_out, not_6_out, not_7_out, not_8_out, not_9_out,
       not_10_out, or_1_out, or_2_out, or_3_out;

  not not_1 (not_1_out, D);
  not not_2 (not_2_out, B);
  not not_3 (not_3_out, D);
  not not_4 (not_4_out, A);
  not not_5 (not_5_out, B);
  not not_6 (not_6_out, C);
  or or_1 (or_1_out, A, B, not_1_out);
  or or_2 (or_2_out, not_2_out, C, not_3_out);
  or or_3 (or_3_out, not_4_out, not_5_out, not_6_out);
  // NOT_Gate not_7 has open pins: in=open, out=not_7_out
  // NOT_Gate not_8 has open pins: in=open, out=not_8_out
  and and_1 (s, or_1_out, or_2_out, or_3_out);
  // NOT_Gate not_9 has open pins: in=open, out=not_9_out
  // NOT_Gate not_10 has open pins: in=open, out=not_10_out

  // Notes on the sheet:
  //   Guia_0604d
  //   Nome: David de Sa Vieira de Faria
  //   Matricula: 699415
  //   nd
  //   nb
  //   nd
  //   na
  //   nb
  //   nc
  //   w1
  //   w2
  //   w3
  //   na
  //   nc
  //   nb
  //   nd
endmodule
