// Logisim project Guia0604e.circ as structural Verilog: 1 circuit, main circuit main
module main (
  input  A,
  input  B,
  input  C,
  input  D,
  output s
);

  wire not_1_out, not_2_out, not_3_out, not_4_out, not_5_out, not_6_out, or_1_out, or_2_out, or_3_out;

  not not_1 (not_1_out, C);
  not not_2 (not_2_out, D);
  not not_3 (not_3_out, B);
  not not_4 (not_4_out, D);
  not not_5 (not_5_out, B);
  not not_6 (not_6_out, C);
  or or_1 (or_1_out, A, not_1_out, not_2_out);
  or or_2 (or_2_out, not_3_out, C, not_4_out);
  or or_3 (or_3_out, not_5_out, not_6_out, D);
  and and_1 (s, or_1_out, or_2_out, or_3_out);

  // Notes on the sheet:
  //   Guia_0604e
  //   Nome: David de Sa Vieira de Faria
  //   Matricula: 699415
  //   nc
  //   nd
  //   nb
  //   nd
  //   nb
  //   nc
  //   w1
  //   w2
  //   w3
endmodule
