// Logisim project Guia0605.circ as structural Verilog: 2 circuits, main circuit main
module main (
  input  X,
  input  Y,
  input  Z,
  output s,
  output s_2
);

  wire and_1_out, and_2_out, and_3_out, and_4_out, and_5_out, not_1_out, not_2_out, not_3_out, not_4_out,
       not_5_out, not_6_out, not_7_out, not_8_out, or_1_out, or_2_out;

  not not_1 (not_1_out, Y);
  not not_2 (not_2_out, X);
  not not_3 (not_3_out, X);
  not not_4 (not_4_out, Y);
  not not_5 (not_5_out, Z);
  or or_1 (or_1_out, not_1_out, not_2_out);
  not not_6 (not_6_out, or_1_out);
  and and_1 (and_1_out, Y, X);
  not not_7 (not_7_out, and_1_out);
  and and_2 (and_2_out, Z, Y);
  and and_3 (and_3_out, X, not_4_out);
  and and_4 (and_4_out, X, not_5_out);
  or or_2 (or_2_out, and_2_out, not_3_out);
  or or_3 (s_2, and_3_out, and_4_out);
  and and_5 (and_5_out, not_6_out, not_7_out);
  not not_8 (not_8_out, or_2_out);
  or or_4 (s, and_5_out, not_8_out);

  // Notes on the sheet:
  //   Guia_0605
  //   Nome: David de Sa Vieira de Faria
  //   Matricula: 699415
  //   w8
  //   w9
  //   w11
  //   w3
  //   w4
  //   Expressao
  //   w5
  //   w6
  //   w10
  //   Expressao Simples
  //   w1
  //   w2
  //   w3
  //   w4
  //   w7
  //   w1
  //   w2
endmodule

module storage (
  input  A,
  input  B,
  input  C,
  input  D
);
endmodule
