// Logisim project Guia0606.circ as structural Verilog: 1 circuit, main circuit main
module main (
  input  X,
  input  Y,
  input  W,
  input  Z,
  output s,
  output s_2
);

  wire and_1_out, and_2_out, and_4_out, not_1_out, not_2_out, not_3_out, not_4_out, not_5_out, not_6_out,
       not_7_out, not_8_out, not_9_out, not_10_out, or_1_out, or_2_out, or_3_out;

  not not_1 (not_1_out, Y);
  not not_2 (not_2_out, X);
  not not_3 (not_3_out, W);
  not not_4 (not_4_out, X);
  not not_5 (not_5_out, Y);
  not not_6 (not_6_out, W);
  not not_7 (not_7_out, Z);
  or or_1 (or_1_out, not_1_out, W, not_2_out);
  not not_8 (not_8_out, or_1_out);
  and and_1 (and_1_out, Y, not_3_out, X);
  not not_9 (not_9_out, and_1_out);
  and and_2 (and_2_out, Z, W, Y);
  or or_2 (or_2_out, not_5_out, not_6_out, not_7_out);
  or or_3 (or_3_out, and_2_out, not_4_out);
  and and_3 (s_2, X, or_2_out);
  and and_4 (and_4_out, not_8_out, not_9_out);
  not not_10 (not_10_out, or_3_out);
  or or_4 (s, and_4_out, not_10_out);

  // Notes on the sheet:
  //   Guia_0606
  //   Nome: David de Sa Vieira de Faria
  //   Matricula: 699415
  //   w8
  //   w9
  //   w10
  //   w12
  //   w2
  //   w3
  //   w4
  //   Expressao
  //   w5
  //   w6
  //   w11
  //   Expressao Simples
  //   w1
  //   w3
  //   w4
  //   w7
  //   w1
  //   w2
endmodule
